// Logisim project OR_CMOS gate.circ as structural Verilog: 2 circuits, main circuit main
module main (
  input  in_1,
  input  in_2,
  input  in_3,
  input  in_4,
  input  in_5,
  input  in_6,
  input  in_7,
  input  in_8,
  output out_9,
  output out_10
);

  wire transistor_2_out, transistor_3_out, transistor_8_out;

  Transistor #(.\type ("n")) transistor_1 (.in(1'b0), .out(in_2), .gate(in_6));
  Transistor transistor_2 (.in(1'b1), .out(transistor_2_out), .gate(in_1));
  Transistor transistor_3 (.in(transistor_2_out), .out(transistor_3_out), .gate(in_3));
  Transistor transistor_4 (.in(transistor_3_out), .out(in_2), .gate(in_4));
  Transistor #(.\type ("n")) transistor_5 (.in(1'b0), .out(in_2), .gate(in_7));
  Transistor #(.\type ("n")) transistor_6 (.in(1'b0), .out(in_2), .gate(in_8));
  Transistor transistor_7 (.in(1'b1), .out(out_9), .gate(in_2));
  Transistor #(.\type ("n")) transistor_8 (.in(out_9), .out(transistor_8_out), .gate(in_2));

  assign in_5 = in_2;
  assign out_10 = in_2;
  // also tied to GND on the sheet: transistor_8_out

  // Notes on the sheet:
  //   NOR GATE
  //   INVERTER
  //   OR CMOS = NOR GATE + INVERTER
endmodule

module Labb2 (
  input  D,
  input  C,
  input  B,
  input  A,
  output Y
);

  wire and_1_out, and_2_out, and_3_out, and_4_out, not_1_out, not_2_out, not_3_out, not_4_out, not_5_out,
       not_6_out, not_7_out;

  not not_1 (not_1_out, D);
  and and_1 (and_1_out, not_1_out, not_2_out, not_3_out);
  not not_2 (not_2_out, C);
  not not_3 (not_3_out, A);
  not not_4 (not_4_out, B);
  and and_2 (and_2_out, not_4_out, not_5_out);
  not not_5 (not_5_out, A);
  not not_6 (not_6_out, D);
  and and_3 (and_3_out, not_6_out, C, not_7_out);
  not not_7 (not_7_out, B);
  and and_4 (and_4_out, D, B, A);
  or or_1 (Y, and_1_out, and_2_out, and_3_out, and_4_out);
endmodule
